# Fritzing sketch devre (saved by Fritzing 1.0.0d)

parts:
  microSD1 = MicroSD Card Module
  SIM800L1 = SIM800L
  Mod1 = sensor_biometrico
  buz1 = Piezo Buzzer
  U3 = ESP8266 NodeMCU LoLin module
  Bat1 = battery_holder_single_18650
  MOD1 = MT3608 Boost No usb
  KF-1 = KF-301 Relay [package=THT]
  M1 = DC Motor [voltage_(max)=6V voltage_(min)=3V]
  Part1 = LCD1602-I2C
  V1 = AMS1777 5V regulator module [package=module]
  Bat2 = battery_holder_single_18650
  Mod2 = 2S-BMS
  M2 = tp5100 [package=THT]
  MOD2 = MT3608 Boost No usb
  Mod3 = 2S-BMS
  M3 = tp5100 [package=THT]
  Part2 = LCD1602-I2C
  KF-2 = KF-301 Relay [package=THT]
  M4 = DC Motor [voltage_(max)=6V voltage_(min)=3V]
  Bat3 = battery_holder_single_18650
  Bat4 = battery_holder_single_18650
  MOD3 = MT3608 Boost No usb
  MOD4 = MT3608 Boost No usb
  buz2 = Piezo Buzzer
  Mod4 = sensor_biometrico
  SIM800L2 = SIM800L
  microSD2 = MicroSD Card Module
  Part4 = Arduino Uno (Rev3)
  U7 = ESP8266-01S [part_number=ESP8266]
  Part5 = Arduino Uno (Rev3)
  U8 = ESP8266-01S [part_number=ESP8266]
  Mod5 = 2S-BMS
  M5 = tp5100 [package=THT]
  Part6 = LCD1602-I2C
  KF-3 = KF-301 Relay [package=THT]
  M6 = DC Motor [voltage_(max)=6V voltage_(min)=3V]
  Bat5 = battery_holder_single_18650
  Bat6 = battery_holder_single_18650
  MOD5 = MT3608 Boost No usb
  MOD6 = MT3608 Boost No usb
  buz3 = Piezo Buzzer
  Mod6 = sensor_biometrico
  SIM800L3 = SIM800L
  microSD3 = MicroSD Card Module
  IC1 = L293D [package=THT]  # not connected
  Part7 = Arduino Uno (Rev3)  # not connected
  U9 = ESP8266-01S [part_number=ESP8266]  # not connected

nets:
  GND: microSD1.GND, SIM800L1.GND, Mod1.GND, buz1.pin_1, U3.GND, MOD1.IN_(-), MOD1.OUT_(-), KF-1.ground, M1.pin_2, Part1.GND, V1.GND-_(input), V1.GND-_(output), Bat2.+#0, Mod2.pin2
  VCC: microSD1.VCC, SIM800L1.VCC, Mod1.VCC, U3.3V3
  N1: microSD1.MISO, U3.D6
  N2: microSD1.MOSI, U3.D7
  N3: microSD1.SCK, U3.D5
  N4: microSD1.CS, U3.D8
  N5: SIM800L1.RXD, U3.D0
  N6: SIM800L1.TXD, U3.D3
  N7: Mod1.TX, U3.TX
  N8: Mod1.RX, U3.RX
  N9: U3.D1, Part1.SCL
  N10: U3.D2, Part1.SDA
  N11: U3.D4, KF-1.signal
  N12: U3.Vin, MOD1.IN_(+), Mod2.pin3#3, M2.+BAT
  N13: Bat1.+#0, Bat2.+#1, Mod2.pin3#4
  N14: Bat1.+#1, Mod2.pin1
  N15: MOD1.OUT_(+), KF-1.C, V1.VIN+
  N16: KF-1.power, Part1.VCC, V1.VOUT+
  N17: KF-1.NC, M1.pin_1
  N18: Mod2.pin3#2, M2.-IN, M2.-BAT, MOD2.OUT_(-)
  N19: M2.+_IN, MOD2.OUT_(+)
  N20: Mod3.pin1, Bat4.+#1
  GND_2: Mod3.pin2, Part2.GND, KF-2.ground, M4.pin_2, Bat3.+#0, MOD4.IN_(-), MOD4.OUT_(-), buz2.pin_1, Mod4.GND, SIM800L2.GND, microSD2.GND, Part4.GND, U7.GND
  N21: Mod3.pin3#2, M3.-IN, M3.-BAT, MOD3.IN_(-), MOD3.OUT_(-)
  N22: Mod3.pin3#3, M3.+BAT, MOD4.IN_(+), Part4.VIN
  N23: Mod3.pin3#4, Bat3.+#1, Bat4.+#0
  N24: M3.+_IN, MOD3.OUT_(+)
  VCC_2: Part2.VCC, KF-2.power, Mod4.VCC, SIM800L2.VCC, SIM800L2.RST, microSD2.VCC, Part4.5V
  N25: Part2.SDA, Part4.A4/SDA
  N26: Part2.SCL, Part4.A5/SCL
  N27: KF-2.signal, Part4.D5_PWM
  N28: KF-2.NC, M4.pin_1
  N29: KF-2.C, MOD4.OUT_(+)
  N30: buz2.pin_2, Part4.D8
  N31: Mod4.TX, Part4.D2
  N32: Mod4.RX, Part4.D3_PWM
  N33: SIM800L2.RXD, Part4.D10_PWM/SS
  N34: SIM800L2.TXD, Part4.D9_PWM
  N35: microSD2.MISO, Part4.D12/MISO
  N36: microSD2.MOSI, Part4.D11_PWM/MOSI
  N37: microSD2.SCK, Part4.D13/SCK
  N38: microSD2.CS, Part4.D4
  N39: Part4.D6_PWM, U7.TXD
  N40: Part4.D7, U7.RXD
  3V3: Part4.3V3, U7.VCC
  N41: Part5.A4/SDA, Part6.SDA
  N42: Part5.A5/SCL, Part6.SCL
  N43: Part5.D8, buz3.pin_2
  N44: Part5.D9_PWM, SIM800L3.TXD
  N45: Part5.D10_PWM/SS, SIM800L3.RXD
  N46: Part5.D11_PWM/MOSI, microSD3.MOSI
  N47: Part5.D12/MISO, microSD3.MISO
  N48: Part5.D13/SCK, microSD3.SCK
  GND_3: Part5.GND, U8.GND, Mod5.pin2, Part6.GND, KF-3.ground, M6.pin_2, Bat5.+#0, MOD6.IN_(-), MOD6.OUT_(-), buz3.pin_1, Mod6.GND, SIM800L3.GND, microSD3.GND
  N49: Part5.D2, Mod6.TX
  N50: Part5.D3_PWM, Mod6.RX
  N51: Part5.D4, microSD3.CS
  N52: Part5.D5_PWM, KF-3.signal
  N53: Part5.D6_PWM, U8.CH_PD, U8.TXD
  N54: Part5.D7, U8.RXD
  3V3_2: Part5.3V3, U8.VCC
  VCC_3: Part5.5V, Part6.VCC, KF-3.power, Mod6.VCC, SIM800L3.VCC, SIM800L3.RST, microSD3.VCC
  N55: Part5.VIN, Mod5.pin3#3, M5.+BAT, MOD6.IN_(+)
  N56: Mod5.pin1, Bat6.+#1
  N57: Mod5.pin3#2, M5.-IN, M5.-BAT, MOD5.OUT_(-)
  N58: Mod5.pin3#4, Bat5.+#1, Bat6.+#0
  N59: M5.+_IN, MOD5.OUT_(+)
  N60: KF-3.NC, M6.pin_1
  N61: KF-3.C, MOD6.OUT_(+)

custom parts:
  SIM800L: SIM800L is a miniature cellular module which allows for GPRS transmission, sending and receiving SMS and making and receiving voice calls. Low cost and small footprint and quad band frequency support make this module perfect solution for any project that require long range connectivity. After connecting power module boots up, searches for cellular network and login automatically. On board LED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
  sensor_biometrico: Adafruit Optical Fingerprint Sensor
  Piezo Buzzer: Part from https://www.nutsvolts.com/magazine/article/november2012_SmileysWorkshop. Breadboard and icon images modified to be 0.3" in spacing and be more similar to the actual physical part.
  ESP8266 NodeMCU LoLin module: ESP8266 based NodeMCU
  battery_holder_single_18650: single 18650 battery holder
  MT3608 Boost No usb: Chip- MT3608 / B6289 DC to DC step up, power booster module. With adjustable output voltage. Current- 2A . || Input voltage- 2V-24V || Output voltage- 5V-28V Input interface- Inversed polarity- NO. || Led indicator- No.
  KF-301 Relay: KF-301
  LCD1602-I2C: A standard character display, usually with 2x16 characters. Comes in many colors with LCM1602 IIC attached.
  AMS1777 5V regulator module: AMS1777 5V regulator module source : https://github.com/ShenTengTu/fritzing_parts/tree/master/voltage%20regulator/AMS1117_5V_regulator_module
  2S-BMS: 2S-BMS LIPO battery charger / protection unit. Note pcb does not match the board as it will likely connect with wires, so pcb is 5 pads suitable for .1in header pins.
  tp5100: Tp5100 battery charger module. Generic ebay type.
